# Fritzing sketch astromech (saved by Fritzing 0.9.3b)
breadboards: 1

parts:
  Part1 = Adafruit HUZZAH32 ESP32 Feather [part_number="Adafruit #3405"]
  Part2 = Breakout Board for Electret Microphone
  ADC1 = MCP3008 [package=dil16]

nets:
  N1: Part1.IO16, ADC1.Dout
  N2: Part1.MISO, ADC1.Din
  N3: Part1.MOSI, ADC1.CLK
  GND: Part1.GND, Part2.GND, ADC1.DGND, ADC1.AGND
  3.3V: Part1.3.3V, Part2.AUD, ADC1.VREF, ADC1.VDD
  N4: Part1.IO14_A6, ADC1.CS/SHDN
  N5: Part2.VCC, ADC1.CH0
